# Fritzing sketch Temperature_Detection_Arduino_UNO (saved by Fritzing 0.9.5d)
breadboards: 1

parts:
  V1 = DC Power [voltage=5]  # not connected
  U1 = MLX90614 [package=to-39]
  Componente1 = Arduino Uno (Rev3) - ICSP
  LED4 = LED - 3mm [color="Red (633nm)" package="3 mm [THT]"]
  LED5 = LED - 3mm [color="Orange (605nm)" package="3 mm [THT]"]
  LED6 = LED - 3mm [color="Green (565nm)" package="3 mm [THT]"]
  R6 = Resistor [tolerance=±5% resistance=470 package=THT]
  R7 = Resistor [tolerance=±5% resistance=470 package=THT]
  hc-sr2 = hc-sr04
  R8 = Resistor [tolerance=±5% resistance=470 package=THT]
  R9 = Resistor [tolerance=±5% resistance=4.7k package=THT]
  R10 = Resistor [tolerance=±5% resistance=4.7k package=THT]

nets:
  N1: U1.SCL_VZ, Componente1.A5/SCL, R9.Pin_1
  N2: U1.PWM_SDA, Componente1.A4/SDA, R10.Pin_1
  VDD: U1.VDD, Componente1.3V3
  GND: U1.VSS, Componente1.GND, R6.Pin_1, R7.Pin_1, hc-sr2.GND, R8.Pin_1
  N3: Componente1.D2, hc-sr2.Trig
  N4: Componente1.D3_PWM, hc-sr2.Echo
  N5: Componente1.D4, LED6.anode
  N6: Componente1.D5_PWM, LED5.anode
  N7: Componente1.D6_PWM, LED4.anode
  5V: Componente1.5V, hc-sr2.VCC, R9.Pin_0, R10.Pin_0
  N8: LED4.cathode, R6.Pin_0
  N9: LED5.cathode, R7.Pin_0
  N10: LED6.cathode, R8.Pin_0
